# Fritzing sketch PNPNMS (saved by Fritzing 0.9.1b)
breadboards: 1

parts:
  Q1 = PNP-Transistor [package="TO92 [THT]"]
  Q2 = NPN-Transistor [package="TO92 [THT]"]
  U1 = attiny85 [package=dip]
  Q3 = NPN-Transistor [package="TO92 [THT]"]
  Q4 = PNP-Transistor [package="TO92 [THT]"]
  U2 = LM358 [package=dip08]
  J1 = shrouded pin header, 12 pins [form="♂ (shrouded male)"]

nets:
  N1: Q1.B, U1.Pin_8
  N2: Q1.C, U1.Pin_7
  N3: Q2.E, U1.Pin_6
  N4: Q2.B, U1.Pin_5
  N5: U1.Pin_3, J1.pin1, J1.pin12
  N6: U1.Pin_4, J1.pin2, J1.pin11
  N7: Q3.E, U2.G$2_-IN
  N8: Q3.B, U2.G$2_+IN
  N9: Q4.B, U2.G$1_V+
  N10: Q4.C, U2.G$2_OUT
  N11: U2.G$1_OUT, J1.pin5, J1.pin8
  N12: U2.G$1_-IN, J1.pin6, J1.pin7
  N13: J1.pin3, J1.pin10
  N14: J1.pin4, J1.pin9
